# Fritzing sketch RadioController (saved by Fritzing 0.9.2b)

parts:
  Part1 = Arduino Mega 2560 (Rev3)
  TRIM_RX_RIGHT = Momentary Switch [package=ksa_sealed_tac_switch]
  POWER = SWITCH_SPDT [package=kps-1290]
  TRIM_RX_LEFT = Momentary Switch [package=ksa_sealed_tac_switch]
  TRIM_LX_RIGHT = Momentary Switch [package=ksa_sealed_tac_switch]
  TRIM_LX_LEFT = Momentary Switch [package=ksa_sealed_tac_switch]
  TRIM_RY_UP = Momentary Switch [package=ksa_sealed_tac_switch]
  TRIM_RY_DOWN = Momentary Switch [package=ksa_sealed_tac_switch]
  TRIM_LY_DOWN = Momentary Switch [package=ksa_sealed_tac_switch]
  TRIM_LY_UP = Momentary Switch [package=ksa_sealed_tac_switch]
  RX = POT [package=pot_alpha_rv16af-20]
  VRB = POT [package=pot_alpha_rv16af-20]
  VRA = POT [package=pot_alpha_rv16af-20]
  RY = POT [package=pot_alpha_rv16af-20]
  LY = POT [package=pot_alpha_rv16af-20]
  LX = POT [package=pot_alpha_rv16af-20]
  NOKIA_5110_(84x48) = Nokia5110LCDModule
  PLUS = Momentary Switch [package=ksa_sealed_tac_switch]
  MENU = Momentary Switch [package=ksa_sealed_tac_switch]
  SEL = Momentary Switch [package=ksa_sealed_tac_switch]
  MINUS = Momentary Switch [package=ksa_sealed_tac_switch]
  SWA = Momentary Switch [package=ksa_sealed_tac_switch]
  SWB = Momentary Switch [package=ksa_sealed_tac_switch]
  SWA1 = Momentary Switch [package=ksa_sealed_tac_switch]
  SWB1 = Momentary Switch [package=ksa_sealed_tac_switch]
  BUZZER = Piezo Speaker
  R1 = Resistor [tolerance=±5% resistance=680 package="2512 [SMD]"]
  R2 = Resistor [tolerance=±5% resistance=10k package="2512 [SMD]"]
  R3 = Resistor [tolerance=±5% resistance=10k package="2512 [SMD]"]
  R4 = Resistor [tolerance=±5% resistance=10k package="2512 [SMD]"]
  R5 = Resistor [tolerance=±5% resistance=10k package="2512 [SMD]"]
  R6 = Resistor [tolerance=±5% resistance=10k package="2512 [SMD]"]
  NRF24L01+_(2_4GHz) = NRF24L01+ Breakout Board
  XY-FST_FS1000A_(433MHz) = CHJ-FST1000M [package=CHJ-FST1000M]
  R7 = Resistor [tolerance=±5% resistance=20k package="2512 [SMD]"]
  R8 = Resistor [tolerance=±5% resistance=10k package="2512 [SMD]"]
  BAT2 = Battery Holders [package=battery-aa-kit]
  BAT7 = Battery Holders [package=battery-aa-kit]
  BAT5 = Battery Holders [package=battery-aa-kit]
  BAT4 = Battery Holders [package=battery-aa-kit]
  BAT8 = Battery Holders [package=battery-aa-kit]
  BAT6 = Battery Holders [package=battery-aa-kit]
  BAT1 = Battery Holders [package=battery-aa-kit]
  BAT3 = Battery Holders [package=battery-aa-kit]
  MPU6050 = MPU-6050 Board GY-521 [form="♀ (female)" package=THT]
  LEVEL_CONVERTER = Logic Level Converter

nets:
  N1: Part1.A0, VRB.S
  N2: Part1.A1, VRA.S
  N3: Part1.A2, RY.S
  N4: Part1.A3, LY.S
  N5: Part1.A4, LX.S
  N6: Part1.A5, RX.S
  N7: Part1.A6, R7.Pin_1, R8.Pin_1
  N8: Part1.D21/SCL, LEVEL_CONVERTER.TX2_HV
  N9: Part1.D20/SDA, LEVEL_CONVERTER.TX_HV
  GND: Part1.GND, TRIM_RX_RIGHT.3, VRB.E, VRA.E, RY.E, LY.E, NOKIA_5110_(84x48).Grnd, NRF24L01+_(2_4GHz).GND, R8.Pin_0, BAT1.-, MPU6050.pin2, LEVEL_CONVERTER.GND
  N10: Part1.D12_PWM, XY-FST_FS1000A_(433MHz).DATA
  N11: Part1.D9_PWM, R1.Pin_1
  N12: Part1.D8_PWM, BUZZER.pin2
  VCC: Part1.3V3, NOKIA_5110_(84x48).Vcc, NRF24L01+_(2_4GHz).VCC, LEVEL_CONVERTER.LV
  5V: Part1.5V, VRB.A, VRA.A, RY.A, XY-FST_FS1000A_(433MHz).+5V
  N13: Part1.VIN, POWER.S
  N14: Part1.D2_PWM, MINUS.4
  N15: Part1.D3_PWM, SEL.2
  N16: Part1.D4_PWM, MENU.4
  N17: Part1.D5_PWM, PLUS.2
  N18: Part1.D6_PWM, NRF24L01+_(2_4GHz).CE
  N19: Part1.D7_PWM, NRF24L01+_(2_4GHz).CS
  N20: Part1.D22, TRIM_LY_UP.2
  N21: Part1.D24, TRIM_LY_DOWN.2
  N22: Part1.D26, TRIM_RY_DOWN.2
  N23: Part1.D28, TRIM_RY_UP.2
  N24: Part1.D30, SWA.2
  N25: Part1.D32, SWB.4
  N26: Part1.D34, SWA1.4
  N27: Part1.D36, SWB1.4
  N28: Part1.D37, TRIM_LX_LEFT.2
  N29: Part1.D38, TRIM_LX_RIGHT.2
  N30: Part1.D40, TRIM_RX_LEFT.2
  N31: Part1.D42, TRIM_RX_RIGHT.2
  N32: Part1.D44, R5.Pin_1
  N33: Part1.D46, R6.Pin_1
  N34: Part1.D48, R4.Pin_1
  N35: Part1.D50, NRF24L01+_(2_4GHz).MISO
  N36: Part1.D51, R3.Pin_1, NRF24L01+_(2_4GHz).MOSI
  N37: Part1.D52, R2.Pin_1, NRF24L01+_(2_4GHz).SCK
  N38: TRIM_RX_RIGHT.1, TRIM_RX_LEFT.3
  N39: POWER.P, R7.Pin_0, BAT6.+
  N40: TRIM_RX_LEFT.1, TRIM_LX_RIGHT.3
  N41: TRIM_LX_RIGHT.1, TRIM_LX_LEFT.3
  N42: TRIM_LX_LEFT.1, TRIM_RY_UP.3
  N43: TRIM_RY_UP.1, TRIM_RY_DOWN.3
  N44: TRIM_RY_DOWN.1, TRIM_LY_DOWN.3
  N45: TRIM_LY_DOWN.1, TRIM_LY_UP.3, BUZZER.pin1
  N46: TRIM_LY_UP.1, PLUS.3
  N47: RX.A, LY.A, LX.A, MPU6050.pin1, LEVEL_CONVERTER.HV
  N48: RX.E, LX.E
  N49: NOKIA_5110_(84x48).SCE, R6.Pin_0
  N50: NOKIA_5110_(84x48).RST, R5.Pin_0
  N51: NOKIA_5110_(84x48).D/C, R4.Pin_0
  N52: NOKIA_5110_(84x48).6_DN_(MOSI), R3.Pin_0
  N53: NOKIA_5110_(84x48).SCLK, R2.Pin_0
  N54: NOKIA_5110_(84x48).LED, R1.Pin_0
  N55: PLUS.1, MENU.3, XY-FST_FS1000A_(433MHz).GND
  N56: MENU.1, SEL.3
  N57: SEL.1, MINUS.3
  N58: MINUS.1, SWB1.3
  N59: SWA.1, SWB.3
  N60: SWA.3, SWB1.1
  N61: SWB.1, SWA1.3
  N62: BAT2.+, BAT3.-
  N63: BAT2.-, BAT1.+
  N64: BAT7.+, BAT8.-
  N65: BAT7.-, BAT4.+
  N66: BAT5.+, BAT6.-
  N67: BAT5.-, BAT8.+
  N68: BAT4.-, BAT3.+
  N69: MPU6050.pin3, LEVEL_CONVERTER.TX2_LV
  N70: MPU6050.pin4, LEVEL_CONVERTER.TX_LV

custom parts:
  : Nokia 5110 LCD with 8 pin. It's a 45mm*45mm module part. Description: The Nokia 5110 is a basic graphic LCD screen for lots of applications. It was originally intended for as a cell phone screen. This one is mounted on an easy to solder PCB. It uses the PCD8544 controller. The PCD8544 is a low power CMOS LCD controller/driver, designed to drive a graphic display of 48 rows and 84 columns. All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
  CHJ-FST1000M: RF LINK
  MPU-6050 Board GY-521: Acelerometro y Giroscopio MPU-6050 Board GY-521
